# Fritzing sketch arduino-radar (saved by Fritzing 1.0.3b)

parts:
  Arduino = Arduino Uno (Rev3)
  Servo = Tower Pro SG90 servo [part_number=101246]
  Ultrasonic_Sensor = HC-SR04 Ultrasonic Distance Sensor

nets:
  N1: Arduino.D9_PWM, Servo.Signal
  N2: Arduino.D11_PWM/MOSI, Ultrasonic_Sensor.ECHO
  N3: Arduino.D12/MISO, Ultrasonic_Sensor.TRIG
  GND: Arduino.GND, Servo.GND, Ultrasonic_Sensor.GND
  3V3: Arduino.3V3, Ultrasonic_Sensor.VCC
  5V: Arduino.5V, Servo.+5V

custom parts:
  Tower Pro SG90 servo: Original file by John De Cristofaro http://www.adafruit.com/products/1449 Adafruit Feedback Servo (Small) Edited by: e-radionica.com 28/9/2015
